# Fritzing sketch raspberrypi1 (saved by Fritzing 0.9.3b)
breadboards: 1

parts:
  Raspberry_Pi1 = Raspberry Pi B+
  LED1 = smd LED [color="Red (633nm)" package="1206 [SMD]"]
  R1 = Resistor [tolerance=±5% resistance=220 package=THT]
  RHT1 = Humidity and Temperature Sensor RHT03
  LED2 = LED - 5mm [color="Red (633nm)" package="5 mm [THT]"]
  R2 = Resistor [tolerance=±5% resistance=220 package=THT]

nets:
  N1: Raspberry_Pi1.GPIO4, RHT1.Data-signal
  N2: Raspberry_Pi1.GPIO24, R2.Pin_1
  N3: Raspberry_Pi1.GPIO23, R1.Pin_1
  N4: Raspberry_Pi1.GND, LED1.cathode, RHT1.GND_2, LED2.cathode
  5V: Raspberry_Pi1.5V, RHT1.Vcc
  N5: LED1.anode, R1.Pin_0
  N6: LED2.anode, R2.Pin_0
